# Fritzing sketch midterm_remote (saved by Fritzing 1.0.2b)
breadboards: 2

parts:
  A2 = Particle - Photon2
  Part2 = 12 NeoPixel Ring [part_number=1643]
  M2 = BMP280
  U2 = ENCODER_RGB [package=encoder_led_2]
  S4 = Pushbutton [package="[SMD]"]
  S3 = Pushbutton [package="[THT]"]
  S2 = Pushbutton [package="[THT]"]
  OLED_I2C3 = OLED 128x64 I2C Monochrome Display
  HC-SR04_Sensor_1 = HC-SR04 Ultrasonic Distance Sensor
  SP1 = SPEAKER [package=pcb_mount_speaker]
  DFRobot_DFPlayer_Mini1 = DFRobot DFPlayer Mini [part_number=DFR0299]

nets:
  VIN: A2.Pin_2, M2.VIN, U2.+, S4.Pin_1, S4.Pin_2, S3.Pin_1, S3.Pin_2, S2.Pin_1, S2.Pin_2, OLED_I2C3.VDD
  GND: A2.Pin_4, Part2.GND, M2.GND, U2.C, OLED_I2C3.GND, HC-SR04_Sensor_1.GND, DFRobot_DFPlayer_Mini1.GND-1, DFRobot_DFPlayer_Mini1.GND-2
  N1: A2.Pin_5, HC-SR04_Sensor_1.ECHO
  N2: A2.Pin_6, DFRobot_DFPlayer_Mini1.IO_2
  N3: A2.Pin_7, DFRobot_DFPlayer_Mini1.IO_1
  N4: A2.Pin_8, U2.B#8
  N5: A2.Pin_9, U2.SW
  N6: A2.Pin_10, U2.G
  N7: A2.Pin_11, U2.R
  N8: A2.Pin_12, DFRobot_DFPlayer_Mini1.BUSY
  N9: A2.Pin_13, HC-SR04_Sensor_1.TRIG
  N10: A2.Pin_14, U2.A
  N11: A2.Pin_15, U2.B#2
  N12: A2.Pin_17, M2.SDA, OLED_I2C3.SDA
  N13: A2.Pin_18, M2.SCL, OLED_I2C3.SCK
  N14: A2.Pin_19, Part2.IN
  N15: A2.Pin_20, S3.Pin_3, S3.Pin_4
  N16: A2.Pin_21, DFRobot_DFPlayer_Mini1.TX
  N17: A2.Pin_22, DFRobot_DFPlayer_Mini1.RX
  N18: A2.Pin_23, S2.Pin_3, S2.Pin_4
  N19: A2.Pin_24, S4.Pin_3, S4.Pin_4
  VCC: A2.Pin_26, Part2.VDD, HC-SR04_Sensor_1.VCC, DFRobot_DFPlayer_Mini1.VCC
  N20: SP1.+, DFRobot_DFPlayer_Mini1.SPK_2
  N21: SP1.-, DFRobot_DFPlayer_Mini1.SPK_1

custom parts:
  Particle - Photon2: The Photon 2 is a microcontroller and Wi-Fi networking developed by particle. Features: 802.11a/b/g/n Wi-Fi, 2.4 GHz and 5 GHz Integrated PCB antenna Integrated U.FL connector for external antenna Integrated RF switch BLE 5 using same antenna as Wi-Fi Realtek RTL8721DM MCU ARM Cortex M33 CPU, 200 MHz 2048 KB (2 MB) user application maximum size 3072 KB (3 MB) of RAM available to user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
  12 NeoPixel Ring: 12 ultra bright smart LED NeoPixels are arranged in a circle with 1.5" (37mm) outer diameter. The rings are 'chainable' - connect the output pin of one to the input pin of another. Use only one microcontroller pin to control as many as you can chain together! Each LED is addressable as the driver chip is inside the LED. Each one has ~18mA constant current drive so the color will be very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
  BMP280: Temperature Humidity Barometric presure Sensor, I2C
  ENCODER_RGB: SparkFun RGB rotary Encoder
